// Digital circuit ImmDecoder.dig as structural Verilog
module ImmDecoder (
  input  [31:0] IW,
  output [63:0] Imm_I,
  output [63:0] Imm_S,
  output [63:0] Imm_J,
  output [63:0] Imm_U,
  output [63:0] Imm_B
);

  BitExtender #(.inputBits(12), .outputBits(64)) _12_Bit (.in(IW[31:20]), .out(Imm_I));
  BitExtender #(.inputBits(12), .outputBits(64)) _12_Bit_2 (.in({IW[31:25], IW[11:7]}), .out(Imm_S));
  BitExtender #(.inputBits(13), .outputBits(64)) _13_Bit (.in({IW[31], IW[7], IW[30:25], IW[11:8], 1'b0}), .out(Imm_B));
  BitExtender #(.inputBits(32), .outputBits(64)) _32_Bit (.in({IW[31:12], {12{1'b0}}}), .out(Imm_U));
  BitExtender #(.inputBits(21), .outputBits(64)) _21_Bit (
    .in({IW[31], IW[19:12], IW[20], IW[30:21], 1'b0}), .out(Imm_J));
endmodule
