// Digital circuit InstDecoder.dig as structural Verilog
module InstDecoder (
  input  [31:0] IW,
  output WDSel,
  output PCSel,
  output [2:0] ALUSrcB,
  output ALUSrcA,
  output [3:0] ALUOp,
  output RFW,
  output [2:0] BROp,
  output [1:0] Sz,
  output Ram,
  output St
);

  wire ADD_eq, ADDI_eq, itype_eq_1_eq, itype_eq_2_eq, itype_eq_3_eq, itype_eq_4_eq, itype_eq_5_eq,
       itype_eq_6_eq, itype_eq_7_eq, itype_eq_8_eq, itype_eq_9_eq, itype_eq_10_eq, itype_eq_11_eq, j_type_eq,
       JALR_eq, LUI_eq, rtype_eq_1_eq, rtype_eq_2_eq, rtype_eq_3_eq, rtype_eq_4_eq, rtype_eq_5_eq,
       shift_1_eq, shift_2_eq, SLL_eq, SRL_eq;
  wire [4:0] INUM_num;

  itype_eq ADDI (.IW_Opcode(IW[6:0]), .Opcode(7'b0010011), .IW_Funct3(IW[14:12]), .Funct3(3'b000), .EQ(ADDI_eq));
  rtype_eq ADD (
    .IW_Opcode(IW[6:0]), .Opcode(7'b0110011), .IW_Funct3(IW[14:12]), .Funct3(3'b000), .IW_Funct7(IW[31:25]),
    .Funct7({7{1'b0}}), .EQ(ADD_eq));
  itype_eq JALR (.IW_Opcode(IW[6:0]), .Opcode(7'b1100111), .IW_Funct3(IW[14:12]), .Funct3(3'b000), .EQ(JALR_eq));
  Shift shift_1 (
    .IW_Opcode(IW[6:0]), .Opcode(7'b0010011), .IW_Funct3(IW[14:12]), .Funct3(3'b001), .IW_Funct6(IW[31:26]),
    .Funct6({6{1'b0}}), .EQ(shift_1_eq));
  rtype_eq SLL (
    .IW_Opcode(IW[6:0]), .Opcode(7'b0110011), .IW_Funct3(IW[14:12]), .Funct3(3'b001), .IW_Funct7(IW[31:25]),
    .Funct7({7{1'b0}}), .EQ(SLL_eq));
  Shift shift_2 (
    .IW_Opcode(IW[6:0]), .Opcode(7'b0010011), .IW_Funct3(IW[14:12]), .Funct3(3'b101), .IW_Funct6(IW[31:26]),
    .Funct6({6{1'b0}}), .EQ(shift_2_eq));
  rtype_eq SRL (
    .IW_Opcode(IW[6:0]), .Opcode(7'b0110011), .IW_Funct3(IW[14:12]), .Funct3(3'b101), .IW_Funct7(IW[31:25]),
    .Funct7({7{1'b0}}), .EQ(SRL_eq));
  itype_eq itype_eq_1 (
    .IW_Opcode(IW[6:0]), .Opcode(7'b1100011), .IW_Funct3(IW[14:12]), .Funct3(3'b000), .EQ(itype_eq_1_eq));
  itype_eq itype_eq_2 (
    .IW_Opcode(IW[6:0]), .Opcode(7'b1100011), .IW_Funct3(IW[14:12]), .Funct3(3'b001), .EQ(itype_eq_2_eq));
  itype_eq itype_eq_3 (
    .IW_Opcode(IW[6:0]), .Opcode(7'b1100011), .IW_Funct3(IW[14:12]), .Funct3(3'b101), .EQ(itype_eq_3_eq));
  itype_eq itype_eq_4 (
    .IW_Opcode(IW[6:0]), .Opcode(7'b1100011), .IW_Funct3(IW[14:12]), .Funct3(3'b100), .EQ(itype_eq_4_eq));
  rtype_eq rtype_eq_1 (
    .IW_Opcode(IW[6:0]), .Opcode(7'b0110011), .IW_Funct3(IW[14:12]), .Funct3(3'b000), .IW_Funct7(IW[31:25]),
    .Funct7(7'b0000001), .EQ(rtype_eq_1_eq));
  itype_eq itype_eq_5 (
    .IW_Opcode(IW[6:0]), .Opcode(7'b0000011), .IW_Funct3(IW[14:12]), .Funct3(3'b000), .EQ(itype_eq_5_eq));
  itype_eq itype_eq_6 (
    .IW_Opcode(IW[6:0]), .Opcode(7'b0000011), .IW_Funct3(IW[14:12]), .Funct3(3'b010), .EQ(itype_eq_6_eq));
  itype_eq itype_eq_7 (
    .IW_Opcode(IW[6:0]), .Opcode(7'b0000011), .IW_Funct3(IW[14:12]), .Funct3(3'b011), .EQ(itype_eq_7_eq));
  itype_eq itype_eq_8 (
    .IW_Opcode(IW[6:0]), .Opcode(7'b0100011), .IW_Funct3(IW[14:12]), .Funct3(3'b000), .EQ(itype_eq_8_eq));
  itype_eq itype_eq_9 (
    .IW_Opcode(IW[6:0]), .Opcode(7'b0100011), .IW_Funct3(IW[14:12]), .Funct3(3'b010), .EQ(itype_eq_9_eq));
  itype_eq itype_eq_10 (
    .IW_Opcode(IW[6:0]), .Opcode(7'b0100011), .IW_Funct3(IW[14:12]), .Funct3(3'b011), .EQ(itype_eq_10_eq));
  rtype_eq rtype_eq_2 (
    .IW_Opcode(IW[6:0]), .Opcode(7'b0110011), .IW_Funct3(IW[14:12]), .Funct3(3'b000), .IW_Funct7(IW[31:25]),
    .Funct7(7'b0100000), .EQ(rtype_eq_2_eq));
  rtype_eq rtype_eq_3 (
    .IW_Opcode(IW[6:0]), .Opcode(7'b0110011), .IW_Funct3(IW[14:12]), .Funct3(3'b111), .IW_Funct7(IW[31:25]),
    .Funct7({7{1'b0}}), .EQ(rtype_eq_3_eq));
  rtype_eq rtype_eq_4 (
    .IW_Opcode(IW[6:0]), .Opcode(7'b0110011), .IW_Funct3(IW[14:12]), .Funct3(3'b110), .IW_Funct7(IW[31:25]),
    .Funct7({7{1'b0}}), .EQ(rtype_eq_4_eq));
  itype_eq itype_eq_11 (
    .IW_Opcode(IW[6:0]), .Opcode(7'b0011011), .IW_Funct3(IW[14:12]), .Funct3(3'b000), .EQ(itype_eq_11_eq));
  rtype_eq rtype_eq_5 (
    .IW_Opcode(IW[6:0]), .Opcode(7'b0111011), .IW_Funct3(IW[14:12]), .Funct3(3'b000), .IW_Funct7(IW[31:25]),
    .Funct7({7{1'b0}}), .EQ(rtype_eq_5_eq));
  Comparator #(.Bits(7)) j_type (.a(IW[6:0]), .b(7'b1101111), .eq(j_type_eq));  // open: gt, lt
  Comparator #(.Bits(7)) LUI (.a(IW[6:0]), .b(7'b0110111), .eq(LUI_eq));  // open: gt, lt
  PriorityEncoder #(.Selector_Bits(5)) INUM (
    .in0(ADDI_eq), .in1(ADD_eq), .in2(j_type_eq), .in3(JALR_eq), .in4(shift_1_eq), .in5(SLL_eq),
    .in6(shift_2_eq), .in7(SRL_eq), .in8(itype_eq_1_eq), .in9(itype_eq_2_eq), .in10(itype_eq_3_eq),
    .in11(itype_eq_4_eq), .in12(rtype_eq_1_eq), .in13(LUI_eq), .in14(itype_eq_5_eq), .in15(itype_eq_6_eq),
    .in16(itype_eq_7_eq), .in17(itype_eq_8_eq), .in18(itype_eq_9_eq), .in19(itype_eq_10_eq),
    .in20(rtype_eq_2_eq), .in21(rtype_eq_3_eq), .in22(rtype_eq_4_eq), .in23(itype_eq_11_eq),
    .in24(rtype_eq_5_eq), .in25(1'b0), .in26(1'b0), .in27(1'b0), .in28(1'b0), .in29(1'b0), .in30(1'b0),
    .in31(1'b0), .num(INUM_num));  // open: any
  ROM #(.AddrBits(5), .Bits(18)) Decoder (
    .A(INUM_num), .sel(1'b1), .D({RFW, ALUOp, ALUSrcA, ALUSrcB, PCSel, WDSel, BROp, Sz, Ram, St}));

  // Notes on the sheet:
  //   contents of Decoder (hex, n*v repeats v):
  //   20200,20000,21580,20380,26200,26000,28200,28000,1810,1820,1830
  //   ,1840,24000,30a00,20206,2020a,2020e,607,60b,60f,22000,2a000,2c000
  //   ,2e200,2e000
endmodule
