// Digital circuit Register File.dig as structural Verilog
module Register_File (
  input  [4:0] RR0,
  input  [4:0] RR1,
  input  CLK,
  input  CLR,
  input  [4:0] WriteReg,
  input  [63:0] WriteData,
  input  WriteEn,
  output [63:0] RD0,
  output [63:0] RD1,
  output [63:0] x0,
  output [63:0] x1,
  output [63:0] x2,
  output [63:0] x3,
  output [63:0] x4,
  output [63:0] x9,
  output [63:0] x6,
  output [63:0] x12,
  output [63:0] x15,
  output [63:0] x18,
  output [63:0] x21,
  output [63:0] x24,
  output [63:0] x27,
  output [63:0] x30,
  output [63:0] x5,
  output [63:0] x7,
  output [63:0] x10,
  output [63:0] x13,
  output [63:0] x16,
  output [63:0] x19,
  output [63:0] x22,
  output [63:0] x25,
  output [63:0] x28,
  output [63:0] x8,
  output [63:0] x11,
  output [63:0] x14,
  output [63:0] x17,
  output [63:0] x20,
  output [63:0] x23,
  output [63:0] x26,
  output [63:0] x29,
  output [63:0] x31
);

  wire decoder_1_out_1, decoder_1_out_2, decoder_1_out_3, decoder_1_out_4, decoder_1_out_5, decoder_1_out_6,
       decoder_1_out_7, decoder_1_out_8, decoder_1_out_9, decoder_1_out_10, decoder_1_out_11,
       decoder_1_out_12, decoder_1_out_13, decoder_1_out_14, decoder_1_out_15, decoder_1_out_16,
       decoder_1_out_17, decoder_1_out_18, decoder_1_out_19, decoder_1_out_20, decoder_1_out_21,
       decoder_1_out_22, decoder_1_out_23, decoder_1_out_24, decoder_1_out_25, decoder_1_out_26,
       decoder_1_out_27, decoder_1_out_28, decoder_1_out_29, decoder_1_out_30, decoder_1_out_31;
  wire [4:0] multiplexer_1_out;

  Multiplexer #(.Bits(5)) multiplexer_1 (.sel(WriteEn), .in_0({5{1'b0}}), .in_1(WriteReg), .out(multiplexer_1_out));
  Decoder #(.Selector_Bits(5)) decoder_1 (
    .sel(multiplexer_1_out), .out_1(decoder_1_out_1), .out_2(decoder_1_out_2), .out_3(decoder_1_out_3),
    .out_4(decoder_1_out_4), .out_5(decoder_1_out_5), .out_6(decoder_1_out_6), .out_7(decoder_1_out_7),
    .out_8(decoder_1_out_8), .out_9(decoder_1_out_9), .out_10(decoder_1_out_10), .out_11(decoder_1_out_11),
    .out_12(decoder_1_out_12), .out_13(decoder_1_out_13), .out_14(decoder_1_out_14),
    .out_15(decoder_1_out_15), .out_16(decoder_1_out_16), .out_17(decoder_1_out_17),
    .out_18(decoder_1_out_18), .out_19(decoder_1_out_19), .out_20(decoder_1_out_20),
    .out_21(decoder_1_out_21), .out_22(decoder_1_out_22), .out_23(decoder_1_out_23),
    .out_24(decoder_1_out_24), .out_25(decoder_1_out_25), .out_26(decoder_1_out_26),
    .out_27(decoder_1_out_27), .out_28(decoder_1_out_28), .out_29(decoder_1_out_29),
    .out_30(decoder_1_out_30), .out_31(decoder_1_out_31));  // open: out_0
  _64_bit_reg _64_bit_reg_1 (.D(WriteData), .CLK(CLK), .CLR(CLR), .EN(decoder_1_out_1), .Q(x1));
  _64_bit_reg _64_bit_reg_2 (.D(WriteData), .CLK(CLK), .CLR(CLR), .EN(decoder_1_out_2), .Q(x2));
  _64_bit_reg _64_bit_reg_3 (.D(WriteData), .CLK(CLK), .CLR(CLR), .EN(decoder_1_out_3), .Q(x3));
  _64_bit_reg _64_bit_reg_4 (.D(WriteData), .CLK(CLK), .CLR(CLR), .EN(decoder_1_out_4), .Q(x4));
  _64_bit_reg _64_bit_reg_5 (.D(WriteData), .CLK(CLK), .CLR(CLR), .EN(decoder_1_out_5), .Q(x5));
  _64_bit_reg _64_bit_reg_6 (.D(WriteData), .CLK(CLK), .CLR(CLR), .EN(decoder_1_out_6), .Q(x6));
  _64_bit_reg _64_bit_reg_7 (.D(WriteData), .CLK(CLK), .CLR(CLR), .EN(decoder_1_out_7), .Q(x7));
  _64_bit_reg _64_bit_reg_8 (.D(WriteData), .CLK(CLK), .CLR(CLR), .EN(decoder_1_out_8), .Q(x8));
  _64_bit_reg _64_bit_reg_9 (.D(WriteData), .CLK(CLK), .CLR(CLR), .EN(decoder_1_out_9), .Q(x9));
  _64_bit_reg _64_bit_reg_10 (.D(WriteData), .CLK(CLK), .CLR(CLR), .EN(decoder_1_out_10), .Q(x10));
  _64_bit_reg _64_bit_reg_11 (.D(WriteData), .CLK(CLK), .CLR(CLR), .EN(decoder_1_out_11), .Q(x11));
  _64_bit_reg _64_bit_reg_12 (.D(WriteData), .CLK(CLK), .CLR(CLR), .EN(decoder_1_out_12), .Q(x12));
  _64_bit_reg _64_bit_reg_13 (.D(WriteData), .CLK(CLK), .CLR(CLR), .EN(decoder_1_out_13), .Q(x13));
  _64_bit_reg _64_bit_reg_14 (.D(WriteData), .CLK(CLK), .CLR(CLR), .EN(decoder_1_out_14), .Q(x14));
  _64_bit_reg _64_bit_reg_15 (.D(WriteData), .CLK(CLK), .CLR(CLR), .EN(decoder_1_out_15), .Q(x15));
  _64_bit_reg _64_bit_reg_16 (.D(WriteData), .CLK(CLK), .CLR(CLR), .EN(decoder_1_out_16), .Q(x16));
  _64_bit_reg _64_bit_reg_17 (.D(WriteData), .CLK(CLK), .CLR(CLR), .EN(decoder_1_out_17), .Q(x17));
  _64_bit_reg _64_bit_reg_18 (.D(WriteData), .CLK(CLK), .CLR(CLR), .EN(decoder_1_out_18), .Q(x18));
  _64_bit_reg _64_bit_reg_19 (.D(WriteData), .CLK(CLK), .CLR(CLR), .EN(decoder_1_out_19), .Q(x19));
  _64_bit_reg _64_bit_reg_20 (.D(WriteData), .CLK(CLK), .CLR(CLR), .EN(decoder_1_out_20), .Q(x20));
  _64_bit_reg _64_bit_reg_21 (.D(WriteData), .CLK(CLK), .CLR(CLR), .EN(decoder_1_out_21), .Q(x21));
  _64_bit_reg _64_bit_reg_22 (.D(WriteData), .CLK(CLK), .CLR(CLR), .EN(decoder_1_out_22), .Q(x22));
  _64_bit_reg _64_bit_reg_23 (.D(WriteData), .CLK(CLK), .CLR(CLR), .EN(decoder_1_out_23), .Q(x23));
  _64_bit_reg _64_bit_reg_24 (.D(WriteData), .CLK(CLK), .CLR(CLR), .EN(decoder_1_out_24), .Q(x24));
  _64_bit_reg _64_bit_reg_25 (.D(WriteData), .CLK(CLK), .CLR(CLR), .EN(decoder_1_out_25), .Q(x25));
  _64_bit_reg _64_bit_reg_26 (.D(WriteData), .CLK(CLK), .CLR(CLR), .EN(decoder_1_out_26), .Q(x26));
  _64_bit_reg _64_bit_reg_27 (.D(WriteData), .CLK(CLK), .CLR(CLR), .EN(decoder_1_out_27), .Q(x27));
  _64_bit_reg _64_bit_reg_28 (.D(WriteData), .CLK(CLK), .CLR(CLR), .EN(decoder_1_out_28), .Q(x28));
  _64_bit_reg _64_bit_reg_29 (.D(WriteData), .CLK(CLK), .CLR(CLR), .EN(decoder_1_out_29), .Q(x29));
  _64_bit_reg _64_bit_reg_30 (.D(WriteData), .CLK(CLK), .CLR(CLR), .EN(decoder_1_out_30), .Q(x30));
  _64_bit_reg _64_bit_reg_31 (.D(WriteData), .CLK(CLK), .CLR(CLR), .EN(decoder_1_out_31), .Q(x31));
  Multiplexer #(.Selector_Bits(5), .Bits(64)) multiplexer_2 (
    .sel(RR0), .in_0({64{1'b0}}), .in_1(x1), .in_2(x2), .in_3(x3), .in_4(x4), .in_5(x5), .in_6(x6),
    .in_7(x7), .in_8(x8), .in_9(x9), .in_10(x10), .in_11(x11), .in_12(x12), .in_13(x13), .in_14(x14),
    .in_15(x15), .in_16(x16), .in_17(x17), .in_18(x18), .in_19(x19), .in_20(x20), .in_21(x21), .in_22(x22),
    .in_23(x23), .in_24(x24), .in_25(x25), .in_26(x26), .in_27(x27), .in_28(x28), .in_29(x29), .in_30(x30),
    .in_31(x31), .out(RD0));
  Multiplexer #(.Selector_Bits(5), .Bits(64)) multiplexer_3 (
    .sel(RR1), .in_0({64{1'b0}}), .in_1(x1), .in_2(x2), .in_3(x3), .in_4(x4), .in_5(x5), .in_6(x6),
    .in_7(x7), .in_8(x8), .in_9(x9), .in_10(x10), .in_11(x11), .in_12(x12), .in_13(x13), .in_14(x14),
    .in_15(x15), .in_16(x16), .in_17(x17), .in_18(x18), .in_19(x19), .in_20(x20), .in_21(x21), .in_22(x22),
    .in_23(x23), .in_24(x24), .in_25(x25), .in_26(x26), .in_27(x27), .in_28(x28), .in_29(x29), .in_30(x30),
    .in_31(x31), .out(RD1));

  assign x0 = {64{1'b0}};
endmodule
