// Digital circuit Shift.dig as structural Verilog
module Shift (
  input  [6:0] IW_Opcode,
  input  [6:0] Opcode,
  input  [2:0] IW_Funct3,
  input  [2:0] Funct3,
  input  [5:0] IW_Funct6,
  input  [5:0] Funct6,
  output EQ
);

  wire add_3_eq, add_6_eq, R_Type_eq;

  Comparator #(.Bits(7)) R_Type (.a(IW_Opcode), .b(Opcode), .eq(R_Type_eq));  // open: gt, lt
  Comparator #(.Bits(3)) add_3 (.a(IW_Funct3), .b(Funct3), .eq(add_3_eq));  // open: gt, lt
  Comparator #(.Bits(6)) add_6 (.a(IW_Funct6), .b(Funct6), .eq(add_6_eq));  // open: gt, lt
  and and_1 (EQ, R_Type_eq, add_3_eq, add_6_eq);
endmodule
