// Digital circuit Write_Ram.dig as structural Verilog
module Write_Ram (
  input  [63:0] D,
  input  [63:0] ADDR,
  input  [1:0] Sz,
  input  [63:0] DNew,
  output [63:0] R
);

  wire [63:0] multiplexer_1_out, multiplexer_2_out;

  Multiplexer #(.Selector_Bits(3), .Bits(64)) multiplexer_1 (
    .sel(ADDR[2:0]), .in_0({D[63:8], DNew[7:0]}), .in_1({D[63:16], DNew[7:0], D[7:0]}),
    .in_2({D[63:24], DNew[7:0], D[15:0]}), .in_3({D[63:32], DNew[7:0], D[23:0]}),
    .in_4({D[63:40], DNew[7:0], D[31:0]}), .in_5({D[63:48], DNew[7:0], D[39:0]}),
    .in_6({D[63:56], DNew[7:0], D[47:0]}), .in_7({DNew[7:0], D[55:0]}), .out(multiplexer_1_out));
  Multiplexer #(.Bits(64)) multiplexer_2 (
    .sel(ADDR[2]), .in_0({D[63:32], DNew[31:0]}), .in_1({DNew[31:0], D[31:0]}), .out(multiplexer_2_out));
  Multiplexer #(.Selector_Bits(2), .Bits(64)) multiplexer_3 (
    .sel(Sz), .in_0({64{1'b0}}), .in_1(multiplexer_1_out), .in_2(multiplexer_2_out), .in_3(DNew), .out(R));

  // Other names for the same wires on the sheet: Byte0[7:0] = D[7:0]; Word0[31:0] = D[31:0]; Byte1[7:0] = D[15:8];
  //   Byte2[7:0] = D[23:16]; Byte3[7:0] = D[31:24]; Byte4[7:0] = D[39:32]; Word1[31:0] = D[63:32];
  //   Byte5[7:0] = D[47:40]; Byte6[7:0] = D[55:48]; Byte7[7:0] = D[63:56]
endmodule
