// Digital circuit project06.dig as structural Verilog
module project06 (
  input  CLK,
  input  [4:0] PROG,
  input  CLR,
  input  EN,
  output DONE,
  output [63:0] A0,
  output [63:0] A1,
  output [63:0] A2,
  output [63:0] A3,
  output [63:0] A4,
  output [63:0] A5,
  output [63:0] A6,
  output [63:0] A7,
  output [63:0] zero,
  output [63:0] RA,
  output [63:0] SP,
  output [63:0] GP,
  output [63:0] TP,
  output [63:0] T0,
  output [63:0] T1,
  output [63:0] T2,
  output [63:0] T6,
  output [63:0] T5,
  output [63:0] T4,
  output [63:0] T3,
  output [63:0] S11,
  output [63:0] S10,
  output [63:0] S9,
  output [63:0] S8,
  output [63:0] S7,
  output [63:0] S6,
  output [63:0] S5,
  output [63:0] S0_FP,
  output [63:0] S1,
  output [63:0] S4,
  output [63:0] S3,
  output [63:0] S2
);

  wire ALUSrcA, and_2_out, CLK_t, PCBr, PCSel, Ram, RFW, St, WDSel;
  wire [1:0] Sz;
  wire [2:0] ALUSrcB, BROp;
  wire [3:0] ALUOp;
  wire [4:0] regdecoder_1_rd, regdecoder_1_rs1, regdecoder_1_rs2;
  wire [6:0] alu_1_r_2;
  wire [7:0] _64_bit_reg_1_q_2;
  wire [31:0] iw;
  wire [63:0] _64_bit_reg_1_q, alu_1_r, immdecoder_1_imm_b, immdecoder_1_imm_i, immdecoder_1_imm_j,
       immdecoder_1_imm_s, immdecoder_1_imm_u, multiplexer_1_out, multiplexer_2_out, multiplexer_3_out,
       multiplexer_4_out, multiplexer_5_out, PC_plus_4_s, ramdualport_1_d, read_ram_1_r, register_file_1_rd0,
       register_file_1_rd1, write_ram_1_r;

  InstDecoder instdecoder_1 (
    .IW(iw), .WDSel(WDSel), .PCSel(PCSel), .ALUSrcB(ALUSrcB), .ALUSrcA(ALUSrcA), .ALUOp(ALUOp), .RFW(RFW),
    .BROp(BROp), .Sz(Sz), .Ram(Ram), .St(St));
  Multiplexer #(.Bits(64)) multiplexer_1 (
    .sel(PCBr), .in_0(PC_plus_4_s), .in_1(multiplexer_5_out), .out(multiplexer_1_out));
  _64_bit_reg _64_bit_reg_1 (
    .D(multiplexer_1_out), .CLK(CLK_t), .CLR(CLR), .EN(EN),
    .Q({_64_bit_reg_1_q[63:10], _64_bit_reg_1_q_2, _64_bit_reg_1_q[1:0]}));
  Comparator #(.Bits(32)) END (.a(iw), .b(32'hc0001073), .eq(DONE));  // open: gt, lt
  inst_mem inst_mem_1 (.PROG(PROG), .ADDR(_64_bit_reg_1_q_2), .IW(iw));
  Add #(.Bits(64)) PC_plus_4 (
    .a({_64_bit_reg_1_q[63:10], _64_bit_reg_1_q_2, _64_bit_reg_1_q[1:0]}), .b(64'h4), .c_i(1'b0),
    .s(PC_plus_4_s));  // open: c_o
  and and_1 (CLK_t, CLK, ~DONE);  // And
  LED led_1 (.in(DONE));
  RegDecoder regdecoder_1 (.IW(iw), .RD(regdecoder_1_rd), .RS1(regdecoder_1_rs1), .RS2(regdecoder_1_rs2));
  Multiplexer #(.Bits(64)) multiplexer_2 (
    .sel(WDSel), .in_0(multiplexer_5_out), .in_1(PC_plus_4_s), .out(multiplexer_2_out));
  and and_2 (and_2_out, RFW, EN);
  Register_File register_file_1 (
    .RR0(regdecoder_1_rs1), .RR1(regdecoder_1_rs2), .WriteData(multiplexer_2_out), .WriteEn(and_2_out),
    .WriteReg(regdecoder_1_rd), .CLK(CLK_t), .CLR(CLR), .RD0(register_file_1_rd0), .RD1(register_file_1_rd1),
    .x0(zero), .x1(RA), .x2(SP), .x3(GP), .x4(TP), .x5(T0), .x6(T1), .x7(T2), .x8(S0_FP), .x9(S1), .x10(A0),
    .x11(A1), .x12(A2), .x13(A3), .x14(A4), .x15(A5), .x16(A6), .x17(A7), .x18(S2), .x19(S3), .x20(S4),
    .x21(S5), .x22(S6), .x23(S7), .x24(S8), .x25(S9), .x26(S10), .x27(S11), .x28(T3), .x29(T4), .x30(T5),
    .x31(T6));
  ImmDecoder immdecoder_1 (
    .Imm_I(immdecoder_1_imm_i), .Imm_S(immdecoder_1_imm_s), .Imm_B(immdecoder_1_imm_b),
    .Imm_U(immdecoder_1_imm_u), .Imm_J(immdecoder_1_imm_j), .IW(iw));
  Multiplexer #(.Bits(64)) multiplexer_3 (
    .sel(ALUSrcA), .in_0(register_file_1_rd0),
    .in_1({_64_bit_reg_1_q[63:10], _64_bit_reg_1_q_2, _64_bit_reg_1_q[1:0]}), .out(multiplexer_3_out));
  Multiplexer #(.Selector_Bits(3), .Bits(64)) multiplexer_4 (
    .sel(ALUSrcB), .in_0(register_file_1_rd1), .in_1(immdecoder_1_imm_i), .in_2(immdecoder_1_imm_j),
    .in_3(immdecoder_1_imm_s), .in_4(immdecoder_1_imm_b), .in_5(immdecoder_1_imm_u), .in_6({64{1'b0}}),
    .in_7({64{1'b0}}), .out(multiplexer_4_out));
  Multiplexer #(.Bits(64)) multiplexer_5 (
    .sel(Ram), .in_0({alu_1_r[63:10], alu_1_r_2, alu_1_r[2:0]}), .in_1(read_ram_1_r), .out(multiplexer_5_out));
  ALU alu_1 (
    .A(multiplexer_3_out), .B(multiplexer_4_out), .ALUOp(ALUOp), .R({alu_1_r[63:10], alu_1_r_2, alu_1_r[2:0]}));
  Branch_Unit branch_unit_1 (.A(register_file_1_rd0), .B(register_file_1_rd1), .BROp(BROp), .PCSel(PCSel), .PCBr(PCBr));
  RAMDualPort #(.AddrBits(7), .Bits(64)) ramdualport_1 (
    .A(alu_1_r_2), .Din(write_ram_1_r), .str(St), .C(CLK_t), .ld(1'b1), .D(ramdualport_1_d));
  Write_Ram write_ram_1 (
    .DNew(register_file_1_rd1), .ADDR({alu_1_r[63:10], alu_1_r_2, alu_1_r[2:0]}), .D(ramdualport_1_d),
    .Sz(Sz), .R(write_ram_1_r));
  Read_Ram read_ram_1 (
    .ADDR({alu_1_r[63:10], alu_1_r_2, alu_1_r[2:0]}), .D(ramdualport_1_d), .Sz(Sz), .R(read_ram_1_r));

  // Other names for the same wires on the sheet: x0[63:0] = zero; x1[63:0] = RA; x2[63:0] = SP; x3[63:0] = GP;
  //   x4[63:0] = TP; x5[63:0] = T0; x6[63:0] = T1; x7[63:0] = T2; x8[63:0] = S0_FP; x9[63:0] = S1; x10[63:0] = A0;
  //   x11[63:0] = A1; x12[63:0] = A2; x13[63:0] = A3; x14[63:0] = A4; x15[63:0] = A5; x16[63:0] = A6; x17[63:0] = A7;
  //   x18[63:0] = S2; x19[63:0] = S3; x20[63:0] = S4; x21[63:0] = S5; x22[63:0] = S6; x23[63:0] = S7; x24[63:0] = S8;
  //   x25[63:0] = S9; x26[63:0] = S10; x27[63:0] = S11; x28[63:0] = T3; x29[63:0] = T4; x30[63:0] = T5;
  //   x31[63:0] = T6

  // Notes on the sheet:
  //   CLK: Hz: 10
endmodule

/* Test case 00-add-r-test:
CLR EN CLK PROG A2
1   0   0   x    x
0   0   0   x    x
while (!(DONE))
0   1   C   0    x
end while
0   1   0   0    3
*/

/* Test case 01-add-i-test:
CLR EN CLK PROG A2
1   0   0   x    x
0   0   0   x    x
while (!(DONE))
0   1   C   1    x
end while
0   1   1   1    3
*/

/* Test case 02-sll-r-test:
CLR EN CLK PROG A0
1   0   0   x    x
0   0   0   x    x
while (!(DONE))
0   1   C   2    x
end while
0   1   0   2    4
*/

/* Test case 03-sll-i-test:
CLR EN CLK PROG A0
1   0   0   x    x
0   0   0   x    x
while (!(DONE))
0   1   C   3    x
end while
0   1   0   3    8
*/

/* Test case 04-srl-r-test:
CLR EN CLK PROG A0
1   0   0   x    x
0   0   0   x    x
while (!(DONE))
0   1   C   4    x
end while
0   1   0   4    4
*/

/* Test case 05-srl-i-test:
CLR EN CLK PROG A0
1   0   0   x    x
0   0   0   x    x
while (!(DONE))
0   1   C   5    x
end while
0   1   0   5    8
*/

/* Test case 06-sd-ld-test:
CLR EN CLK PROG A0
1   0   0   x    x
0   0   0   x    x
while (!(DONE))
0   1   C   6    x
end while
0   1   0   6    99
*/

/* Test case 07-sw-lw-test:
CLR EN CLK PROG A0
1   0   0   x    x
0   0   0   x    x
while (!(DONE))
0   1   C   7    x
end while
0   1   0   7    99
*/

/* Test case 08-jal-test:
EN CLR CLK PROG A0
1  1   0   x    x
1  0   0   x    x
while (!(DONE))
1  0   C   8    x
end while
1  0   0   8    3
*/

/* Test case 09-j-test:
EN CLR CLK PROG A0
1  1   0   x    x
1  0   0   x    x
while (!(DONE))
1  0   C   9    x
end while
1  0   0   9    1
*/

/* Test case 10-beq-test:
EN CLR CLK PROG A0
1  1   0   x    x
1  0   0   x    x
while (!(DONE))
1  0   C   10   x
end while
1  0   0   10   1
*/

/* Test case 11-blt-test:
EN CLR CLK PROG A0
1  1   0   x    x
1  0   0   x    x
while (!(DONE))
1  0   C   11   x
end while
1  0   0   11   1
*/

/* Test case 12-bge-test:
EN CLR CLK PROG A0
1  1   0   x    x
1  0   0   x    x
while (!(DONE))
1  0   C   12   x
end while
1  0   0   12   2
*/

/* Test case 13-mul-test:
EN CLR CLK PROG A0
1  1   0   x    x
1  0   0   x    x
while (!(DONE))
1  0   C   13   x
end while
1  0   0   13   9
*/

/* Test case 14-lui-test:
EN CLR CLK PROG A0
1  1   0   x    x
1  0   0   x    x
while (!(DONE))
1  0   C   14   x
end while
1  0   0   14   4096
*/

/* Test case 15-sb-lb-test:
CLR EN CLK PROG A0
1   0   0   x    x
0   0   0   x    x
while (!(DONE))
0   1   C   15    x
end while
0   1   0   15    99
*/

/* Test case 16-quadratic-test:
CLR EN CLK PROG A0
1   0   0   x    x
0   0   0   x    x
while (!(DONE))
0   1   C   16    x
end while
0   1   0   16    25
*/

/* Test case 17-get-bitseq-test:
CLR EN CLK PROG A0
1   0   0   x    x
0   0   0   x    x
while (!(DONE))
0   1   C   17   x
end while
0   1   0   17   6
*/

/* Test case 18-max3-test:
CLR EN CLK PROG A0
1   0   0   x    x
0   0   0   x    x
while (!(DONE))
0   1   C   18   x
end while
0   1   0   18   2
*/

/* Test case 19-fib-rec-test:
CLR EN CLK PROG A0
1   0   0   x    x
0   0   0   x    x
while (!(DONE))
0   1   C   19   x
end while
0   1   0   19   55
*/

/* Test case 20-is-pal-test:
CLR EN CLK PROG A0
1   0   0   x    x
0   0   0   x    x
while (!(DONE))
0   1   C   20   x
end while
0   1   0   20   1
*/

/* Test case 21-to-upper-test:
CLR EN CLK PROG A0
1   0   0   x    x
0   0   0   x    x
while (!(DONE))
0   1   C   21   x
end while
0   1   0   21   5066355251797426176
*/

/* Test case 22-sort-test:
CLR EN CLK PROG A0 A1 A2
1   0   0   x    x    x    x
0   0   0   x    x    x    x
while (!(DONE))
0   1   C   22   x    x    x
end while
0   1   0   22   51539607562 34359738374 17179869186
*/

/* Test case 23-merge-sort-test:
CLR EN CLK PROG A0 A1 A2
1   0   0   x    x    x    x
0   0   0   x    x    x    x
while (!(DONE))
0   1   C   23   x    x    x
end while
0   1   0   23   8589934596 25769803784 42949672972
*/
