// Digital circuit rtype_eq.dig as structural Verilog
module rtype_eq (
  input  [6:0] IW_Opcode,
  input  [6:0] Opcode,
  input  [2:0] IW_Funct3,
  input  [2:0] Funct3,
  input  [6:0] IW_Funct7,
  input  [6:0] Funct7,
  output EQ
);

  wire add_3_eq, add_7_eq, R_Type_eq;

  Comparator #(.Bits(7)) R_Type (.a(IW_Opcode), .b(Opcode), .eq(R_Type_eq));  // open: gt, lt
  Comparator #(.Bits(3)) add_3 (.a(IW_Funct3), .b(Funct3), .eq(add_3_eq));  // open: gt, lt
  Comparator #(.Bits(7)) add_7 (.a(IW_Funct7), .b(Funct7), .eq(add_7_eq));  // open: gt, lt
  and and_1 (EQ, R_Type_eq, add_3_eq, add_7_eq);
endmodule
